// Digital circuit ALU.dig as structural Verilog
module ALU (
);

  wire _7447_1_pin3, _7447_1_pin9, _7447_1_pin10, _7447_1_pin11, _7447_1_pin12, _7447_1_pin13, _7447_1_pin14,
       _7447_1_pin15, _7447_2_pin3, _7447_2_pin9, _7447_2_pin10, _7447_2_pin11, _7447_2_pin12, _7447_2_pin13,
       _7447_2_pin14, _7447_2_pin15, _7447_3_pin3, _7447_3_pin9, _7447_3_pin10, _7447_3_pin11, _7447_3_pin12,
       _7447_3_pin13, _7447_3_pin14, _7447_3_pin15, _7447_4_pin3, _7447_4_pin9, _7447_4_pin10, _7447_4_pin11,
       _7447_4_pin12, _7447_4_pin13, _7447_4_pin14, _7447_4_pin15, _7447_5_pin3, _7447_5_pin9, _7447_5_pin10,
       _7447_5_pin11, _7447_5_pin12, _7447_5_pin13, _7447_5_pin14, _7447_5_pin15, _7447_6_pin3, _7447_6_pin9,
       _7447_6_pin10, _7447_6_pin11, _7447_6_pin12, _7447_6_pin13, _7447_6_pin14, _7447_6_pin15,
       _7447_7_pin3, _7447_7_pin9, _7447_7_pin10, _7447_7_pin11, _7447_7_pin12, _7447_7_pin13, _7447_7_pin14,
       _7447_7_pin15, A0_out, A1_out, add_1_c_o, add_1_s, add_2_c_o, add_2_s, and_1_out, and_2_out,
       and_3_out, and_4_out, and_5_out, and_6_out, and_7_out, and_8_out, and_9_out, and_10_out, and_11_out,
       and_12_out, and_13_out, and_14_out, and_15_out, and_16_out, B0_out, B1_out, demultiplexer_1_out_0,
       demultiplexer_1_out_1, demultiplexer_1_out_2, demultiplexer_2_out_0, demultiplexer_2_out_1,
       demultiplexer_2_out_2, demultiplexer_3_out_0, demultiplexer_3_out_1, demultiplexer_3_out_2,
       demultiplexer_4_out_0, demultiplexer_4_out_1, demultiplexer_4_out_2, not_1_out, not_2_out, not_3_out,
       not_4_out, or_1_out, or_2_out, or_3_out, or_4_out, xor_1_out, xor_2_out, xor_3_out, xor_4_out;
  wire [1:0] _7447_1_pin7;

  DipSwitch B0 (.out(B0_out));
  DipSwitch B1 (.out(B1_out));
  _7447 _7447_1 (
    .pin1(_7447_1_pin7[1]), .pin2(1'b0), .pin3(_7447_1_pin3), .pin4(_7447_1_pin3), .pin5(_7447_1_pin3),
    .pin6(1'b0), .pin7(_7447_1_pin7[0]), .pin8(1'b0), .pin9(_7447_1_pin9), .pin10(_7447_1_pin10),
    .pin11(_7447_1_pin11), .pin12(_7447_1_pin12), .pin13(_7447_1_pin13), .pin14(_7447_1_pin14),
    .pin15(_7447_1_pin15), .pin16(_7447_1_pin3));
  DipSwitch A0 (.out(A0_out));
  DipSwitch A1 (.out(A1_out));
  PowerSupply powersupply_1 (.VDD(_7447_1_pin3), .GND(1'b0));
  Seven_Seg #(.commonCathode("true"), .commonConnectionType("anode")) seven_seg_1 (
    .a(_7447_1_pin13), .b(_7447_1_pin12), .c(_7447_1_pin11), .d(_7447_1_pin10), .e(_7447_1_pin9),
    .f(_7447_1_pin15), .g(_7447_1_pin14), .dp(1'b0), .common(_7447_1_pin3));
  DipSwitch O1 (.out(_7447_1_pin7[1]));
  DipSwitch O0 (.out(_7447_1_pin7[0]));
  Demultiplexer #(.Selector_Bits(2)) demultiplexer_1 (
    .sel(_7447_1_pin7), .in(B0_out), .out_0(demultiplexer_1_out_0), .out_1(demultiplexer_1_out_1),
    .out_2(demultiplexer_1_out_2));  // open: out_3
  Demultiplexer #(.Selector_Bits(2)) demultiplexer_2 (
    .sel(_7447_1_pin7), .in(A0_out), .out_0(demultiplexer_2_out_0), .out_1(demultiplexer_2_out_1),
    .out_2(demultiplexer_2_out_2));  // open: out_3
  Demultiplexer #(.Selector_Bits(2)) demultiplexer_3 (
    .sel(_7447_1_pin7), .in(B1_out), .out_0(demultiplexer_3_out_0), .out_1(demultiplexer_3_out_1),
    .out_2(demultiplexer_3_out_2));  // open: out_3
  Demultiplexer #(.Selector_Bits(2)) demultiplexer_4 (
    .sel(_7447_1_pin7), .in(A1_out), .out_0(demultiplexer_4_out_0), .out_1(demultiplexer_4_out_1),
    .out_2(demultiplexer_4_out_2));  // open: out_3
  not not_1 (not_1_out, demultiplexer_1_out_1);
  not not_2 (not_2_out, demultiplexer_2_out_1);
  _7447 _7447_2 (
    .pin1(B1_out), .pin2(1'b0), .pin3(_7447_2_pin3), .pin4(_7447_2_pin3), .pin5(_7447_2_pin3), .pin6(1'b0),
    .pin7(A1_out), .pin8(1'b0), .pin9(_7447_2_pin9), .pin10(_7447_2_pin10), .pin11(_7447_2_pin11),
    .pin12(_7447_2_pin12), .pin13(_7447_2_pin13), .pin14(_7447_2_pin14), .pin15(_7447_2_pin15),
    .pin16(_7447_2_pin3));
  PowerSupply powersupply_2 (.VDD(_7447_2_pin3), .GND(1'b0));
  xor xor_1 (xor_1_out, demultiplexer_4_out_2, demultiplexer_2_out_2);
  xor xor_2 (xor_2_out, demultiplexer_1_out_2, demultiplexer_3_out_2);
  Seven_Seg #(.commonCathode("true"), .commonConnectionType("anode")) seven_seg_2 (
    .a(_7447_2_pin13), .b(_7447_2_pin12), .c(_7447_2_pin11), .d(_7447_2_pin10), .e(_7447_2_pin9),
    .f(_7447_2_pin15), .g(_7447_2_pin14), .dp(1'b0), .common(_7447_2_pin3));
  and and_1 (and_1_out, demultiplexer_2_out_0, demultiplexer_4_out_0);
  and and_2 (and_2_out, demultiplexer_1_out_0, demultiplexer_4_out_0);
  and and_3 (and_3_out, demultiplexer_2_out_0, demultiplexer_3_out_0);
  and and_4 (and_4_out, demultiplexer_1_out_0, demultiplexer_3_out_0);
  and and_5 (and_5_out, demultiplexer_4_out_1, not_1_out);
  and and_6 (and_6_out, demultiplexer_4_out_1, demultiplexer_3_out_1);
  and and_7 (and_7_out, not_2_out, demultiplexer_3_out_1);
  and and_8 (and_8_out, demultiplexer_3_out_1, demultiplexer_2_out_1, not_1_out);
  and and_9 (and_9_out, demultiplexer_3_out_1, not_3_out, demultiplexer_2_out_1, demultiplexer_1_out_1);
  not not_3 (not_3_out, demultiplexer_4_out_1);
  and and_10 (and_10_out, not_2_out, demultiplexer_4_out_1);
  and and_11 (and_11_out, demultiplexer_1_out_1, demultiplexer_4_out_1, not_4_out);
  not not_4 (not_4_out, demultiplexer_3_out_1);
  Add add_1 (.a(and_2_out), .b(and_3_out), .c_i(1'b0), .s(add_1_s), .c_o(add_1_c_o));
  or or_1 (or_1_out, and_10_out, and_11_out);
  xor xor_3 (xor_3_out, xor_1_out, 1'b0);
  and and_12 (and_12_out, 1'b0, xor_1_out);
  and and_13 (and_13_out, demultiplexer_2_out_2, demultiplexer_4_out_2);
  xor xor_4 (xor_4_out, xor_2_out, or_3_out);
  and and_14 (and_14_out, or_3_out, xor_2_out);
  and and_15 (and_15_out, demultiplexer_3_out_2, demultiplexer_1_out_2);
  Add add_2 (.a(add_1_c_o), .b(and_4_out), .c_i(1'b0), .s(add_2_s), .c_o(add_2_c_o));
  _7447 _7447_3 (
    .pin1(B0_out), .pin2(1'b0), .pin3(_7447_3_pin3), .pin4(_7447_3_pin3), .pin5(_7447_3_pin3), .pin6(1'b0),
    .pin7(A0_out), .pin8(1'b0), .pin9(_7447_3_pin9), .pin10(_7447_3_pin10), .pin11(_7447_3_pin11),
    .pin12(_7447_3_pin12), .pin13(_7447_3_pin13), .pin14(_7447_3_pin14), .pin15(_7447_3_pin15),
    .pin16(_7447_3_pin3));
  or or_2 (or_2_out, and_5_out, and_6_out, and_7_out);
  or or_3 (or_3_out, and_12_out, and_13_out);
  or or_4 (or_4_out, and_14_out, and_15_out);
  PowerSupply powersupply_3 (.VDD(_7447_3_pin3), .GND(1'b0));
  and and_16 (and_16_out, not_2_out, not_1_out);
  Seven_Seg #(.commonCathode("true"), .commonConnectionType("anode")) seven_seg_3 (
    .a(_7447_3_pin13), .b(_7447_3_pin12), .c(_7447_3_pin11), .d(_7447_3_pin10), .e(_7447_3_pin9),
    .f(_7447_3_pin15), .g(_7447_3_pin14), .dp(1'b0), .common(_7447_3_pin3));
  _7447 _7447_4 (
    .pin1(add_1_s), .pin2(add_2_s), .pin3(_7447_4_pin3), .pin4(_7447_4_pin3), .pin5(_7447_4_pin3),
    .pin6(add_2_c_o), .pin7(and_1_out), .pin8(1'b0), .pin9(_7447_4_pin9), .pin10(_7447_4_pin10),
    .pin11(_7447_4_pin11), .pin12(_7447_4_pin12), .pin13(_7447_4_pin13), .pin14(_7447_4_pin14),
    .pin15(_7447_4_pin15), .pin16(_7447_4_pin3));
  _7447 _7447_5 (
    .pin1(and_8_out), .pin2(1'b0), .pin3(_7447_5_pin3), .pin4(_7447_5_pin3), .pin5(_7447_5_pin3),
    .pin6(1'b0), .pin7(or_2_out), .pin8(1'b0), .pin9(_7447_5_pin9), .pin10(_7447_5_pin10),
    .pin11(_7447_5_pin11), .pin12(_7447_5_pin12), .pin13(_7447_5_pin13), .pin14(_7447_5_pin14),
    .pin15(_7447_5_pin15), .pin16(_7447_5_pin3));
  _7447 _7447_6 (
    .pin1(and_9_out), .pin2(1'b0), .pin3(_7447_6_pin3), .pin4(_7447_6_pin3), .pin5(_7447_6_pin3),
    .pin6(1'b0), .pin7(or_1_out), .pin8(1'b0), .pin9(_7447_6_pin9), .pin10(_7447_6_pin10),
    .pin11(_7447_6_pin11), .pin12(_7447_6_pin12), .pin13(_7447_6_pin13), .pin14(_7447_6_pin14),
    .pin15(_7447_6_pin15), .pin16(_7447_6_pin3));
  _7447 _7447_7 (
    .pin1(xor_4_out), .pin2(or_4_out), .pin3(_7447_7_pin3), .pin4(_7447_7_pin3), .pin5(_7447_7_pin3),
    .pin6(1'b0), .pin7(xor_3_out), .pin8(1'b0), .pin9(_7447_7_pin9), .pin10(_7447_7_pin10),
    .pin11(_7447_7_pin11), .pin12(_7447_7_pin12), .pin13(_7447_7_pin13), .pin14(_7447_7_pin14),
    .pin15(_7447_7_pin15), .pin16(_7447_7_pin3));
  PowerSupply powersupply_4 (.VDD(_7447_4_pin3), .GND(1'b0));
  PowerSupply powersupply_5 (.VDD(_7447_6_pin3), .GND(1'b0));
  Seven_Seg #(.commonCathode("true"), .commonConnectionType("anode")) seven_seg_4 (
    .a(_7447_4_pin13), .b(_7447_4_pin12), .c(_7447_4_pin11), .d(_7447_4_pin10), .e(_7447_4_pin9),
    .f(_7447_4_pin15), .g(_7447_4_pin14), .dp(1'b0), .common(_7447_4_pin3));
  PowerSupply powersupply_6 (.VDD(_7447_5_pin3), .GND(1'b0));
  Seven_Seg #(.commonCathode("true"), .commonConnectionType("anode")) seven_seg_5 (
    .a(_7447_5_pin13), .b(_7447_5_pin12), .c(_7447_5_pin11), .d(_7447_5_pin10), .e(_7447_5_pin9),
    .f(_7447_5_pin15), .g(_7447_5_pin14), .dp(1'b0), .common(_7447_5_pin3));
  Seven_Seg #(.commonCathode("true"), .commonConnectionType("anode")) seven_seg_6 (
    .a(_7447_6_pin13), .b(_7447_6_pin12), .c(_7447_6_pin11), .d(_7447_6_pin10), .e(_7447_6_pin9),
    .f(_7447_6_pin15), .g(_7447_6_pin14), .dp(1'b0), .common(_7447_6_pin3));
  PowerSupply powersupply_7 (.VDD(_7447_7_pin3), .GND(1'b0));
  Seven_Seg #(.commonCathode("true"), .commonConnectionType("anode")) seven_seg_7 (
    .a(_7447_7_pin13), .b(_7447_7_pin12), .c(_7447_7_pin11), .d(_7447_7_pin10), .e(_7447_7_pin9),
    .f(_7447_7_pin15), .g(_7447_7_pin14), .dp(1'b0), .common(_7447_7_pin3));
  LED led_1 (.in(and_16_out));

  // Notes on the sheet:
  //   OPCODE
  //   B0
  //   A0
  //   B1
  //   A1
  //   A
  //   Mutliplication
  //   B
  //   Remainder
  //   Quotient
  //   FLAG
endmodule
